# Fritzing sketch Arduino MIDI Out 4 Switches (saved by Fritzing 0.9.3b)
breadboards: 1

parts:
  Bauteil1 = Arduino Uno (Rev3)
  S1 = Pushbutton [package="[THT]"]
  S2 = Pushbutton [package="[THT]"]
  S3 = Pushbutton [package="[THT]"]
  S4 = Pushbutton [package="[THT]"]
  LED1 = LED - 5mm [color="Red (633nm)" package="5 mm [THT]"]
  LED2 = LED - 5mm [color="Red (633nm)" package="5 mm [THT]"]
  LED3 = LED - 5mm [color="Red (633nm)" package="5 mm [THT]"]
  LED4 = LED - 5mm [color="Red (633nm)" package="5 mm [THT]"]
  R1 = Resistor [tolerance=±5% resistance=220 package=THT]
  R2 = Resistor [tolerance=±5% resistance=220 package=THT]
  R3 = Resistor [tolerance=±5% resistance=220 package=THT]
  R4 = Resistor [tolerance=±5% resistance=220 package=THT]
  U1 = MIDI_CONN_FEMALE [package=din_5_female]
  R5 = Resistor [tolerance=±5% resistance=220 package=THT]
  R6 = Resistor [tolerance=±5% resistance=220 package=THT]

nets:
  N1: Bauteil1.D8, S2.Pin_3, S2.Pin_4
  N2: Bauteil1.D9_PWM, LED2.anode
  N3: Bauteil1.D10_PWM/SS, S1.Pin_3, S1.Pin_4
  N4: Bauteil1.D11_PWM/MOSI, LED1.anode
  N5: Bauteil1.D1/TX, R6.Pin_1
  N6: Bauteil1.D4, S4.Pin_3, S4.Pin_4
  N7: Bauteil1.D5_PWM, LED4.anode
  N8: Bauteil1.D6_PWM, S3.Pin_3, S3.Pin_4
  N9: Bauteil1.D7, LED3.anode
  N10: Bauteil1.5V, R5.Pin_1
  N11: Bauteil1.GND, S1.Pin_1, S1.Pin_2, S2.Pin_1, S2.Pin_2, S3.Pin_1, S3.Pin_2, S4.Pin_1, S4.Pin_2, R1.Pin_1, R2.Pin_1, R3.Pin_1, R4.Pin_1, U1.NC1
  N12: LED1.cathode, R1.Pin_0
  N13: LED2.cathode, R2.Pin_0
  N14: LED3.cathode, R3.Pin_0
  N15: LED4.cathode, R4.Pin_0
  N16: U1.MIDI_IN, R6.Pin_0
  N17: U1.MIDI_OUT, R5.Pin_0
